// Logisim project RV.circ as structural Verilog
module EXE_ALU_BarrelShifter (
  input  CLKi,
  input  RIGHTi,
  input  [4:0] SHAMTi,
  input  [31:0] D,
  input  ARITHi,
  output [31:0] Q
);

  wire register_1_q, register_4_q, register_5_q, register_8_q, register_9_q, register_12_q, register_13_q,
       register_14_q, register_16_q, Stage1_righto, Stage1_signo, Stage2_righto, Stage2_signo, Stage3_righto,
       Stage3_signo, Stage4_righto, Stage4_shamto, Stage4_signo;
  wire [1:0] register_10_q, Stage3_shamto;
  wire [2:0] register_6_q, Stage2_shamto;
  wire [3:0] register_2_q, Stage1_shamto;
  wire [31:0] register_3_q, register_7_q, register_11_q, register_15_q, Stage1_q, Stage2_q, Stage3_q,
       Stage4_q;

  EXE_ALU_BarrelShifter_Stage1 Stage1 (
    .RIGHTi(RIGHTi), .SHAMTi(SHAMTi), .D(D), .ARITHi(ARITHi), .RIGHTo(Stage1_righto), .SHAMTo(Stage1_shamto),
    .Q(Stage1_q), .SIGNo(Stage1_signo));
  Register #(.width(1)) register_1 (.D(Stage1_righto), .en(1'b1), .clk(CLKi), .Q(register_1_q), .clr(1'b0));
  Register #(.width(4)) register_2 (.D(Stage1_shamto), .en(1'b1), .clk(CLKi), .Q(register_2_q), .clr(1'b0));
  Register #(.width(32)) register_3 (.D(Stage1_q), .en(1'b1), .clk(CLKi), .Q(register_3_q), .clr(1'b0));
  Register #(.width(1)) register_4 (.D(Stage1_signo), .en(1'b1), .clk(CLKi), .Q(register_4_q), .clr(1'b0));
  Register #(.width(1)) register_5 (.D(Stage2_righto), .en(1'b1), .clk(CLKi), .Q(register_5_q), .clr(1'b0));
  EXE_ALU_BarrelShifter_Stage2 Stage2 (
    .RIGHTi(register_1_q), .SHAMTi(register_2_q), .D(register_3_q), .SIGNi(register_4_q),
    .RIGHTo(Stage2_righto), .SHAMTo(Stage2_shamto), .Q(Stage2_q), .SIGNo(Stage2_signo));
  Register #(.width(3)) register_6 (.D(Stage2_shamto), .en(1'b1), .clk(CLKi), .Q(register_6_q), .clr(1'b0));
  Register #(.width(32)) register_7 (.D(Stage2_q), .en(1'b1), .clk(CLKi), .Q(register_7_q), .clr(1'b0));
  Register #(.width(1)) register_8 (.D(Stage2_signo), .en(1'b1), .clk(CLKi), .Q(register_8_q), .clr(1'b0));
  EXE_ALU_BarrelShifter_Stage3 Stage3 (
    .RIGHTi(register_5_q), .SHAMTi(register_6_q), .D(register_7_q), .SIGNi(register_8_q),
    .RIGHTo(Stage3_righto), .SHAMTo(Stage3_shamto), .Q(Stage3_q), .SIGNo(Stage3_signo));
  Register #(.width(1)) register_9 (.D(Stage3_righto), .en(1'b1), .clk(CLKi), .Q(register_9_q), .clr(1'b0));
  Register #(.width(2)) register_10 (.D(Stage3_shamto), .en(1'b1), .clk(CLKi), .Q(register_10_q), .clr(1'b0));
  Register #(.width(32)) register_11 (.D(Stage3_q), .en(1'b1), .clk(CLKi), .Q(register_11_q), .clr(1'b0));
  Register #(.width(1)) register_12 (.D(Stage3_signo), .en(1'b1), .clk(CLKi), .Q(register_12_q), .clr(1'b0));
  EXE_ALU_BarrelShifter_Stage4 Stage4 (
    .RIGHTi(register_9_q), .SHAMTi(register_10_q), .D(register_11_q), .SIGNi(register_12_q),
    .RIGHTo(Stage4_righto), .SHAMTo(Stage4_shamto), .Q(Stage4_q), .SIGNo(Stage4_signo));
  Register #(.width(1)) register_13 (.D(Stage4_righto), .en(1'b1), .clk(CLKi), .Q(register_13_q), .clr(1'b0));
  Register #(.width(1)) register_14 (.D(Stage4_shamto), .en(1'b1), .clk(CLKi), .Q(register_14_q), .clr(1'b0));
  Register #(.width(32)) register_15 (.D(Stage4_q), .en(1'b1), .clk(CLKi), .Q(register_15_q), .clr(1'b0));
  Register #(.width(1)) register_16 (.D(Stage4_signo), .en(1'b1), .clk(CLKi), .Q(register_16_q), .clr(1'b0));
  EXE_ALU_BarrelShifter_Stage5 Stage5 (
    .RIGHTi(register_13_q), .SHAMTi(register_14_q), .D(register_15_q), .SIGNi(register_16_q), .Q(Q));
endmodule

module EXE_ALU_BarrelShifter_Stage1 (
  input  RIGHTi,
  input  [4:0] SHAMTi,
  input  [31:0] D,
  input  ARITHi,
  output RIGHTo,
  output [3:0] SHAMTo,
  output [31:0] Q,
  output SIGNo
);

  and and_1 (SIGNo, D[31], ARITHi);
  Multiplexer #(.select(2)) multiplexer_1 (
    .in0(D[0]), .in1(D[0]), .in2(1'b0), .in3(D[16]), .out(Q[0]), .sel({SHAMTi[4], RIGHTi}));
  Multiplexer #(.select(2)) multiplexer_2 (
    .in0(D[1]), .in1(D[1]), .in2(1'b0), .in3(D[17]), .out(Q[1]), .sel({SHAMTi[4], RIGHTi}));
  Multiplexer #(.select(2)) multiplexer_3 (
    .in0(D[2]), .in1(D[2]), .in2(1'b0), .in3(D[18]), .out(Q[2]), .sel({SHAMTi[4], RIGHTi}));
  Multiplexer #(.select(2)) multiplexer_4 (
    .in0(D[3]), .in1(D[3]), .in2(1'b0), .in3(D[19]), .out(Q[3]), .sel({SHAMTi[4], RIGHTi}));
  Multiplexer #(.select(2)) multiplexer_5 (
    .in0(D[4]), .in1(D[4]), .in2(1'b0), .in3(D[20]), .out(Q[4]), .sel({SHAMTi[4], RIGHTi}));
  Multiplexer #(.select(2)) multiplexer_6 (
    .in0(D[5]), .in1(D[5]), .in2(1'b0), .in3(D[21]), .out(Q[5]), .sel({SHAMTi[4], RIGHTi}));
  Multiplexer #(.select(2)) multiplexer_7 (
    .in0(D[6]), .in1(D[6]), .in2(1'b0), .in3(D[22]), .out(Q[6]), .sel({SHAMTi[4], RIGHTi}));
  Multiplexer #(.select(2)) multiplexer_8 (
    .in0(D[7]), .in1(D[7]), .in2(1'b0), .in3(D[23]), .out(Q[7]), .sel({SHAMTi[4], RIGHTi}));
  Multiplexer #(.select(2)) multiplexer_9 (
    .in0(D[8]), .in1(D[8]), .in2(1'b0), .in3(D[24]), .out(Q[8]), .sel({SHAMTi[4], RIGHTi}));
  Multiplexer #(.select(2)) multiplexer_10 (
    .in0(D[9]), .in1(D[9]), .in2(1'b0), .in3(D[25]), .out(Q[9]), .sel({SHAMTi[4], RIGHTi}));
  Multiplexer #(.select(2)) multiplexer_11 (
    .in0(D[10]), .in1(D[10]), .in2(1'b0), .in3(D[26]), .out(Q[10]), .sel({SHAMTi[4], RIGHTi}));
  Multiplexer #(.select(2)) multiplexer_12 (
    .in0(D[11]), .in1(D[11]), .in2(1'b0), .in3(D[27]), .out(Q[11]), .sel({SHAMTi[4], RIGHTi}));
  Multiplexer #(.select(2)) multiplexer_13 (
    .in0(D[12]), .in1(D[12]), .in2(1'b0), .in3(D[28]), .out(Q[12]), .sel({SHAMTi[4], RIGHTi}));
  Multiplexer #(.select(2)) multiplexer_14 (
    .in0(D[13]), .in1(D[13]), .in2(1'b0), .in3(D[29]), .out(Q[13]), .sel({SHAMTi[4], RIGHTi}));
  Multiplexer #(.select(2)) multiplexer_15 (
    .in0(D[14]), .in1(D[14]), .in2(1'b0), .in3(D[30]), .out(Q[14]), .sel({SHAMTi[4], RIGHTi}));
  Multiplexer #(.select(2)) multiplexer_16 (
    .in0(D[15]), .in1(D[15]), .in2(1'b0), .in3(D[31]), .out(Q[15]), .sel({SHAMTi[4], RIGHTi}));
  Multiplexer #(.select(2)) multiplexer_17 (
    .in0(D[16]), .in1(D[16]), .in2(D[0]), .in3(SIGNo), .out(Q[16]), .sel({SHAMTi[4], RIGHTi}));
  Multiplexer #(.select(2)) multiplexer_18 (
    .in0(D[17]), .in1(D[17]), .in2(D[1]), .in3(SIGNo), .out(Q[17]), .sel({SHAMTi[4], RIGHTi}));
  Multiplexer #(.select(2)) multiplexer_19 (
    .in0(D[18]), .in1(D[18]), .in2(D[2]), .in3(SIGNo), .out(Q[18]), .sel({SHAMTi[4], RIGHTi}));
  Multiplexer #(.select(2)) multiplexer_20 (
    .in0(D[19]), .in1(D[19]), .in2(D[3]), .in3(SIGNo), .out(Q[19]), .sel({SHAMTi[4], RIGHTi}));
  Multiplexer #(.select(2)) multiplexer_21 (
    .in0(D[20]), .in1(D[20]), .in2(D[4]), .in3(SIGNo), .out(Q[20]), .sel({SHAMTi[4], RIGHTi}));
  Multiplexer #(.select(2)) multiplexer_22 (
    .in0(D[21]), .in1(D[21]), .in2(D[5]), .in3(SIGNo), .out(Q[21]), .sel({SHAMTi[4], RIGHTi}));
  Multiplexer #(.select(2)) multiplexer_23 (
    .in0(D[22]), .in1(D[22]), .in2(D[6]), .in3(SIGNo), .out(Q[22]), .sel({SHAMTi[4], RIGHTi}));
  Multiplexer #(.select(2)) multiplexer_24 (
    .in0(D[23]), .in1(D[23]), .in2(D[7]), .in3(SIGNo), .out(Q[23]), .sel({SHAMTi[4], RIGHTi}));
  Multiplexer #(.select(2)) multiplexer_25 (
    .in0(D[24]), .in1(D[24]), .in2(D[8]), .in3(SIGNo), .out(Q[24]), .sel({SHAMTi[4], RIGHTi}));
  Multiplexer #(.select(2)) multiplexer_26 (
    .in0(D[25]), .in1(D[25]), .in2(D[9]), .in3(SIGNo), .out(Q[25]), .sel({SHAMTi[4], RIGHTi}));
  Multiplexer #(.select(2)) multiplexer_27 (
    .in0(D[26]), .in1(D[26]), .in2(D[10]), .in3(SIGNo), .out(Q[26]), .sel({SHAMTi[4], RIGHTi}));
  Multiplexer #(.select(2)) multiplexer_28 (
    .in0(D[27]), .in1(D[27]), .in2(D[11]), .in3(SIGNo), .out(Q[27]), .sel({SHAMTi[4], RIGHTi}));
  Multiplexer #(.select(2)) multiplexer_29 (
    .in0(D[28]), .in1(D[28]), .in2(D[12]), .in3(SIGNo), .out(Q[28]), .sel({SHAMTi[4], RIGHTi}));
  Multiplexer #(.select(2)) multiplexer_30 (
    .in0(D[29]), .in1(D[29]), .in2(D[13]), .in3(SIGNo), .out(Q[29]), .sel({SHAMTi[4], RIGHTi}));
  Multiplexer #(.select(2)) multiplexer_31 (
    .in0(D[30]), .in1(D[30]), .in2(D[14]), .in3(SIGNo), .out(Q[30]), .sel({SHAMTi[4], RIGHTi}));
  Multiplexer #(.select(2)) multiplexer_32 (
    .in0(D[31]), .in1(D[31]), .in2(D[15]), .in3(SIGNo), .out(Q[31]), .sel({SHAMTi[4], RIGHTi}));

  assign RIGHTo = RIGHTi;
  assign SHAMTo = SHAMTi[3:0];
endmodule

module EXE_ALU_BarrelShifter_Stage2 (
  input  RIGHTi,
  input  [3:0] SHAMTi,
  input  [31:0] D,
  input  SIGNi,
  output RIGHTo,
  output [2:0] SHAMTo,
  output [31:0] Q,
  output SIGNo
);

  Multiplexer #(.select(2)) multiplexer_1 (
    .in0(D[0]), .in1(D[0]), .in2(1'b0), .in3(D[8]), .out(Q[0]), .sel({SHAMTi[3], RIGHTi}));
  Multiplexer #(.select(2)) multiplexer_2 (
    .in0(D[1]), .in1(D[1]), .in2(1'b0), .in3(D[9]), .out(Q[1]), .sel({SHAMTi[3], RIGHTi}));
  Multiplexer #(.select(2)) multiplexer_3 (
    .in0(D[2]), .in1(D[2]), .in2(1'b0), .in3(D[10]), .out(Q[2]), .sel({SHAMTi[3], RIGHTi}));
  Multiplexer #(.select(2)) multiplexer_4 (
    .in0(D[3]), .in1(D[3]), .in2(1'b0), .in3(D[11]), .out(Q[3]), .sel({SHAMTi[3], RIGHTi}));
  Multiplexer #(.select(2)) multiplexer_5 (
    .in0(D[4]), .in1(D[4]), .in2(1'b0), .in3(D[12]), .out(Q[4]), .sel({SHAMTi[3], RIGHTi}));
  Multiplexer #(.select(2)) multiplexer_6 (
    .in0(D[5]), .in1(D[5]), .in2(1'b0), .in3(D[13]), .out(Q[5]), .sel({SHAMTi[3], RIGHTi}));
  Multiplexer #(.select(2)) multiplexer_7 (
    .in0(D[6]), .in1(D[6]), .in2(1'b0), .in3(D[14]), .out(Q[6]), .sel({SHAMTi[3], RIGHTi}));
  Multiplexer #(.select(2)) multiplexer_8 (
    .in0(D[7]), .in1(D[7]), .in2(1'b0), .in3(D[15]), .out(Q[7]), .sel({SHAMTi[3], RIGHTi}));
  Multiplexer #(.select(2)) multiplexer_9 (
    .in0(D[8]), .in1(D[8]), .in2(D[0]), .in3(D[16]), .out(Q[8]), .sel({SHAMTi[3], RIGHTi}));
  Multiplexer #(.select(2)) multiplexer_10 (
    .in0(D[9]), .in1(D[9]), .in2(D[1]), .in3(D[17]), .out(Q[9]), .sel({SHAMTi[3], RIGHTi}));
  Multiplexer #(.select(2)) multiplexer_11 (
    .in0(D[10]), .in1(D[10]), .in2(D[2]), .in3(D[18]), .out(Q[10]), .sel({SHAMTi[3], RIGHTi}));
  Multiplexer #(.select(2)) multiplexer_12 (
    .in0(D[11]), .in1(D[11]), .in2(D[3]), .in3(D[19]), .out(Q[11]), .sel({SHAMTi[3], RIGHTi}));
  Multiplexer #(.select(2)) multiplexer_13 (
    .in0(D[12]), .in1(D[12]), .in2(D[4]), .in3(D[20]), .out(Q[12]), .sel({SHAMTi[3], RIGHTi}));
  Multiplexer #(.select(2)) multiplexer_14 (
    .in0(D[13]), .in1(D[13]), .in2(D[5]), .in3(D[21]), .out(Q[13]), .sel({SHAMTi[3], RIGHTi}));
  Multiplexer #(.select(2)) multiplexer_15 (
    .in0(D[14]), .in1(D[14]), .in2(D[6]), .in3(D[22]), .out(Q[14]), .sel({SHAMTi[3], RIGHTi}));
  Multiplexer #(.select(2)) multiplexer_16 (
    .in0(D[15]), .in1(D[15]), .in2(D[7]), .in3(D[23]), .out(Q[15]), .sel({SHAMTi[3], RIGHTi}));
  Multiplexer #(.select(2)) multiplexer_17 (
    .in0(D[16]), .in1(D[16]), .in2(D[8]), .in3(D[24]), .out(Q[16]), .sel({SHAMTi[3], RIGHTi}));
  Multiplexer #(.select(2)) multiplexer_18 (
    .in0(D[17]), .in1(D[17]), .in2(D[9]), .in3(D[25]), .out(Q[17]), .sel({SHAMTi[3], RIGHTi}));
  Multiplexer #(.select(2)) multiplexer_19 (
    .in0(D[18]), .in1(D[18]), .in2(D[10]), .in3(D[26]), .out(Q[18]), .sel({SHAMTi[3], RIGHTi}));
  Multiplexer #(.select(2)) multiplexer_20 (
    .in0(D[19]), .in1(D[19]), .in2(D[11]), .in3(D[27]), .out(Q[19]), .sel({SHAMTi[3], RIGHTi}));
  Multiplexer #(.select(2)) multiplexer_21 (
    .in0(D[20]), .in1(D[20]), .in2(D[12]), .in3(D[28]), .out(Q[20]), .sel({SHAMTi[3], RIGHTi}));
  Multiplexer #(.select(2)) multiplexer_22 (
    .in0(D[21]), .in1(D[21]), .in2(D[13]), .in3(D[29]), .out(Q[21]), .sel({SHAMTi[3], RIGHTi}));
  Multiplexer #(.select(2)) multiplexer_23 (
    .in0(D[22]), .in1(D[22]), .in2(D[14]), .in3(D[30]), .out(Q[22]), .sel({SHAMTi[3], RIGHTi}));
  Multiplexer #(.select(2)) multiplexer_24 (
    .in0(D[23]), .in1(D[23]), .in2(D[15]), .in3(D[31]), .out(Q[23]), .sel({SHAMTi[3], RIGHTi}));
  Multiplexer #(.select(2)) multiplexer_25 (
    .in0(D[24]), .in1(D[24]), .in2(D[16]), .in3(SIGNi), .out(Q[24]), .sel({SHAMTi[3], RIGHTi}));
  Multiplexer #(.select(2)) multiplexer_26 (
    .in0(D[25]), .in1(D[25]), .in2(D[17]), .in3(SIGNi), .out(Q[25]), .sel({SHAMTi[3], RIGHTi}));
  Multiplexer #(.select(2)) multiplexer_27 (
    .in0(D[26]), .in1(D[26]), .in2(D[18]), .in3(SIGNi), .out(Q[26]), .sel({SHAMTi[3], RIGHTi}));
  Multiplexer #(.select(2)) multiplexer_28 (
    .in0(D[27]), .in1(D[27]), .in2(D[19]), .in3(SIGNi), .out(Q[27]), .sel({SHAMTi[3], RIGHTi}));
  Multiplexer #(.select(2)) multiplexer_29 (
    .in0(D[28]), .in1(D[28]), .in2(D[20]), .in3(SIGNi), .out(Q[28]), .sel({SHAMTi[3], RIGHTi}));
  Multiplexer #(.select(2)) multiplexer_30 (
    .in0(D[29]), .in1(D[29]), .in2(D[21]), .in3(SIGNi), .out(Q[29]), .sel({SHAMTi[3], RIGHTi}));
  Multiplexer #(.select(2)) multiplexer_31 (
    .in0(D[30]), .in1(D[30]), .in2(D[22]), .in3(SIGNi), .out(Q[30]), .sel({SHAMTi[3], RIGHTi}));
  Multiplexer #(.select(2)) multiplexer_32 (
    .in0(D[31]), .in1(D[31]), .in2(D[23]), .in3(SIGNi), .out(Q[31]), .sel({SHAMTi[3], RIGHTi}));

  assign RIGHTo = RIGHTi;
  assign SHAMTo = SHAMTi[2:0];
  assign SIGNo = SIGNi;
endmodule

module EXE_ALU_BarrelShifter_Stage3 (
  input  RIGHTi,
  input  [2:0] SHAMTi,
  input  [31:0] D,
  input  SIGNi,
  output RIGHTo,
  output [1:0] SHAMTo,
  output [31:0] Q,
  output SIGNo
);

  Multiplexer #(.select(2)) multiplexer_1 (
    .in0(D[0]), .in1(D[0]), .in2(1'b0), .in3(D[4]), .out(Q[0]), .sel({SHAMTi[2], RIGHTi}));
  Multiplexer #(.select(2)) multiplexer_2 (
    .in0(D[1]), .in1(D[1]), .in2(1'b0), .in3(D[5]), .out(Q[1]), .sel({SHAMTi[2], RIGHTi}));
  Multiplexer #(.select(2)) multiplexer_3 (
    .in0(D[2]), .in1(D[2]), .in2(1'b0), .in3(D[6]), .out(Q[2]), .sel({SHAMTi[2], RIGHTi}));
  Multiplexer #(.select(2)) multiplexer_4 (
    .in0(D[3]), .in1(D[3]), .in2(1'b0), .in3(D[7]), .out(Q[3]), .sel({SHAMTi[2], RIGHTi}));
  Multiplexer #(.select(2)) multiplexer_5 (
    .in0(D[4]), .in1(D[4]), .in2(D[0]), .in3(D[8]), .out(Q[4]), .sel({SHAMTi[2], RIGHTi}));
  Multiplexer #(.select(2)) multiplexer_6 (
    .in0(D[5]), .in1(D[5]), .in2(D[1]), .in3(D[9]), .out(Q[5]), .sel({SHAMTi[2], RIGHTi}));
  Multiplexer #(.select(2)) multiplexer_7 (
    .in0(D[6]), .in1(D[6]), .in2(D[2]), .in3(D[10]), .out(Q[6]), .sel({SHAMTi[2], RIGHTi}));
  Multiplexer #(.select(2)) multiplexer_8 (
    .in0(D[7]), .in1(D[7]), .in2(D[3]), .in3(D[11]), .out(Q[7]), .sel({SHAMTi[2], RIGHTi}));
  Multiplexer #(.select(2)) multiplexer_9 (
    .in0(D[8]), .in1(D[8]), .in2(D[4]), .in3(D[12]), .out(Q[8]), .sel({SHAMTi[2], RIGHTi}));
  Multiplexer #(.select(2)) multiplexer_10 (
    .in0(D[9]), .in1(D[9]), .in2(D[5]), .in3(D[13]), .out(Q[9]), .sel({SHAMTi[2], RIGHTi}));
  Multiplexer #(.select(2)) multiplexer_11 (
    .in0(D[10]), .in1(D[10]), .in2(D[6]), .in3(D[14]), .out(Q[10]), .sel({SHAMTi[2], RIGHTi}));
  Multiplexer #(.select(2)) multiplexer_12 (
    .in0(D[11]), .in1(D[11]), .in2(D[7]), .in3(D[15]), .out(Q[11]), .sel({SHAMTi[2], RIGHTi}));
  Multiplexer #(.select(2)) multiplexer_13 (
    .in0(D[12]), .in1(D[12]), .in2(D[8]), .in3(D[16]), .out(Q[12]), .sel({SHAMTi[2], RIGHTi}));
  Multiplexer #(.select(2)) multiplexer_14 (
    .in0(D[13]), .in1(D[13]), .in2(D[9]), .in3(D[17]), .out(Q[13]), .sel({SHAMTi[2], RIGHTi}));
  Multiplexer #(.select(2)) multiplexer_15 (
    .in0(D[14]), .in1(D[14]), .in2(D[10]), .in3(D[18]), .out(Q[14]), .sel({SHAMTi[2], RIGHTi}));
  Multiplexer #(.select(2)) multiplexer_16 (
    .in0(D[15]), .in1(D[15]), .in2(D[11]), .in3(D[19]), .out(Q[15]), .sel({SHAMTi[2], RIGHTi}));
  Multiplexer #(.select(2)) multiplexer_17 (
    .in0(D[16]), .in1(D[16]), .in2(D[12]), .in3(D[20]), .out(Q[16]), .sel({SHAMTi[2], RIGHTi}));
  Multiplexer #(.select(2)) multiplexer_18 (
    .in0(D[17]), .in1(D[17]), .in2(D[13]), .in3(D[21]), .out(Q[17]), .sel({SHAMTi[2], RIGHTi}));
  Multiplexer #(.select(2)) multiplexer_19 (
    .in0(D[18]), .in1(D[18]), .in2(D[14]), .in3(D[22]), .out(Q[18]), .sel({SHAMTi[2], RIGHTi}));
  Multiplexer #(.select(2)) multiplexer_20 (
    .in0(D[19]), .in1(D[19]), .in2(D[15]), .in3(D[23]), .out(Q[19]), .sel({SHAMTi[2], RIGHTi}));
  Multiplexer #(.select(2)) multiplexer_21 (
    .in0(D[20]), .in1(D[20]), .in2(D[16]), .in3(D[24]), .out(Q[20]), .sel({SHAMTi[2], RIGHTi}));
  Multiplexer #(.select(2)) multiplexer_22 (
    .in0(D[21]), .in1(D[21]), .in2(D[17]), .in3(D[25]), .out(Q[21]), .sel({SHAMTi[2], RIGHTi}));
  Multiplexer #(.select(2)) multiplexer_23 (
    .in0(D[22]), .in1(D[22]), .in2(D[18]), .in3(D[26]), .out(Q[22]), .sel({SHAMTi[2], RIGHTi}));
  Multiplexer #(.select(2)) multiplexer_24 (
    .in0(D[23]), .in1(D[23]), .in2(D[19]), .in3(D[27]), .out(Q[23]), .sel({SHAMTi[2], RIGHTi}));
  Multiplexer #(.select(2)) multiplexer_25 (
    .in0(D[24]), .in1(D[24]), .in2(D[20]), .in3(D[28]), .out(Q[24]), .sel({SHAMTi[2], RIGHTi}));
  Multiplexer #(.select(2)) multiplexer_26 (
    .in0(D[25]), .in1(D[25]), .in2(D[21]), .in3(D[29]), .out(Q[25]), .sel({SHAMTi[2], RIGHTi}));
  Multiplexer #(.select(2)) multiplexer_27 (
    .in0(D[26]), .in1(D[26]), .in2(D[22]), .in3(D[30]), .out(Q[26]), .sel({SHAMTi[2], RIGHTi}));
  Multiplexer #(.select(2)) multiplexer_28 (
    .in0(D[27]), .in1(D[27]), .in2(D[23]), .in3(D[31]), .out(Q[27]), .sel({SHAMTi[2], RIGHTi}));
  Multiplexer #(.select(2)) multiplexer_29 (
    .in0(D[28]), .in1(D[28]), .in2(D[24]), .in3(SIGNi), .out(Q[28]), .sel({SHAMTi[2], RIGHTi}));
  Multiplexer #(.select(2)) multiplexer_30 (
    .in0(D[29]), .in1(D[29]), .in2(D[25]), .in3(SIGNi), .out(Q[29]), .sel({SHAMTi[2], RIGHTi}));
  Multiplexer #(.select(2)) multiplexer_31 (
    .in0(D[30]), .in1(D[30]), .in2(D[26]), .in3(SIGNi), .out(Q[30]), .sel({SHAMTi[2], RIGHTi}));
  Multiplexer #(.select(2)) multiplexer_32 (
    .in0(D[31]), .in1(D[31]), .in2(D[27]), .in3(SIGNi), .out(Q[31]), .sel({SHAMTi[2], RIGHTi}));

  assign RIGHTo = RIGHTi;
  assign SHAMTo = SHAMTi[1:0];
  assign SIGNo = SIGNi;
endmodule

module EXE_ALU_BarrelShifter_Stage4 (
  input  RIGHTi,
  input  [1:0] SHAMTi,
  input  [31:0] D,
  input  SIGNi,
  output RIGHTo,
  output SHAMTo,
  output [31:0] Q,
  output SIGNo
);

  Multiplexer #(.select(2)) multiplexer_1 (
    .in0(D[0]), .in1(D[0]), .in2(1'b0), .in3(D[2]), .out(Q[0]), .sel({SHAMTi[1], RIGHTi}));
  Multiplexer #(.select(2)) multiplexer_2 (
    .in0(D[1]), .in1(D[1]), .in2(1'b0), .in3(D[3]), .out(Q[1]), .sel({SHAMTi[1], RIGHTi}));
  Multiplexer #(.select(2)) multiplexer_3 (
    .in0(D[2]), .in1(D[2]), .in2(D[0]), .in3(D[4]), .out(Q[2]), .sel({SHAMTi[1], RIGHTi}));
  Multiplexer #(.select(2)) multiplexer_4 (
    .in0(D[3]), .in1(D[3]), .in2(D[1]), .in3(D[5]), .out(Q[3]), .sel({SHAMTi[1], RIGHTi}));
  Multiplexer #(.select(2)) multiplexer_5 (
    .in0(D[4]), .in1(D[4]), .in2(D[2]), .in3(D[6]), .out(Q[4]), .sel({SHAMTi[1], RIGHTi}));
  Multiplexer #(.select(2)) multiplexer_6 (
    .in0(D[5]), .in1(D[5]), .in2(D[3]), .in3(D[7]), .out(Q[5]), .sel({SHAMTi[1], RIGHTi}));
  Multiplexer #(.select(2)) multiplexer_7 (
    .in0(D[6]), .in1(D[6]), .in2(D[4]), .in3(D[8]), .out(Q[6]), .sel({SHAMTi[1], RIGHTi}));
  Multiplexer #(.select(2)) multiplexer_8 (
    .in0(D[7]), .in1(D[7]), .in2(D[5]), .in3(D[9]), .out(Q[7]), .sel({SHAMTi[1], RIGHTi}));
  Multiplexer #(.select(2)) multiplexer_9 (
    .in0(D[8]), .in1(D[8]), .in2(D[6]), .in3(D[10]), .out(Q[8]), .sel({SHAMTi[1], RIGHTi}));
  Multiplexer #(.select(2)) multiplexer_10 (
    .in0(D[9]), .in1(D[9]), .in2(D[7]), .in3(D[11]), .out(Q[9]), .sel({SHAMTi[1], RIGHTi}));
  Multiplexer #(.select(2)) multiplexer_11 (
    .in0(D[10]), .in1(D[10]), .in2(D[8]), .in3(D[12]), .out(Q[10]), .sel({SHAMTi[1], RIGHTi}));
  Multiplexer #(.select(2)) multiplexer_12 (
    .in0(D[11]), .in1(D[11]), .in2(D[9]), .in3(D[13]), .out(Q[11]), .sel({SHAMTi[1], RIGHTi}));
  Multiplexer #(.select(2)) multiplexer_13 (
    .in0(D[12]), .in1(D[12]), .in2(D[10]), .in3(D[14]), .out(Q[12]), .sel({SHAMTi[1], RIGHTi}));
  Multiplexer #(.select(2)) multiplexer_14 (
    .in0(D[13]), .in1(D[13]), .in2(D[11]), .in3(D[15]), .out(Q[13]), .sel({SHAMTi[1], RIGHTi}));
  Multiplexer #(.select(2)) multiplexer_15 (
    .in0(D[14]), .in1(D[14]), .in2(D[12]), .in3(D[16]), .out(Q[14]), .sel({SHAMTi[1], RIGHTi}));
  Multiplexer #(.select(2)) multiplexer_16 (
    .in0(D[15]), .in1(D[15]), .in2(D[13]), .in3(D[17]), .out(Q[15]), .sel({SHAMTi[1], RIGHTi}));
  Multiplexer #(.select(2)) multiplexer_17 (
    .in0(D[16]), .in1(D[16]), .in2(D[14]), .in3(D[18]), .out(Q[16]), .sel({SHAMTi[1], RIGHTi}));
  Multiplexer #(.select(2)) multiplexer_18 (
    .in0(D[17]), .in1(D[17]), .in2(D[15]), .in3(D[19]), .out(Q[17]), .sel({SHAMTi[1], RIGHTi}));
  Multiplexer #(.select(2)) multiplexer_19 (
    .in0(D[18]), .in1(D[18]), .in2(D[16]), .in3(D[20]), .out(Q[18]), .sel({SHAMTi[1], RIGHTi}));
  Multiplexer #(.select(2)) multiplexer_20 (
    .in0(D[19]), .in1(D[19]), .in2(D[17]), .in3(D[21]), .out(Q[19]), .sel({SHAMTi[1], RIGHTi}));
  Multiplexer #(.select(2)) multiplexer_21 (
    .in0(D[20]), .in1(D[20]), .in2(D[18]), .in3(D[22]), .out(Q[20]), .sel({SHAMTi[1], RIGHTi}));
  Multiplexer #(.select(2)) multiplexer_22 (
    .in0(D[21]), .in1(D[21]), .in2(D[19]), .in3(D[23]), .out(Q[21]), .sel({SHAMTi[1], RIGHTi}));
  Multiplexer #(.select(2)) multiplexer_23 (
    .in0(D[22]), .in1(D[22]), .in2(D[20]), .in3(D[24]), .out(Q[22]), .sel({SHAMTi[1], RIGHTi}));
  Multiplexer #(.select(2)) multiplexer_24 (
    .in0(D[23]), .in1(D[23]), .in2(D[21]), .in3(D[25]), .out(Q[23]), .sel({SHAMTi[1], RIGHTi}));
  Multiplexer #(.select(2)) multiplexer_25 (
    .in0(D[24]), .in1(D[24]), .in2(D[22]), .in3(D[26]), .out(Q[24]), .sel({SHAMTi[1], RIGHTi}));
  Multiplexer #(.select(2)) multiplexer_26 (
    .in0(D[25]), .in1(D[25]), .in2(D[23]), .in3(D[27]), .out(Q[25]), .sel({SHAMTi[1], RIGHTi}));
  Multiplexer #(.select(2)) multiplexer_27 (
    .in0(D[26]), .in1(D[26]), .in2(D[24]), .in3(D[28]), .out(Q[26]), .sel({SHAMTi[1], RIGHTi}));
  Multiplexer #(.select(2)) multiplexer_28 (
    .in0(D[27]), .in1(D[27]), .in2(D[25]), .in3(D[29]), .out(Q[27]), .sel({SHAMTi[1], RIGHTi}));
  Multiplexer #(.select(2)) multiplexer_29 (
    .in0(D[28]), .in1(D[28]), .in2(D[26]), .in3(D[30]), .out(Q[28]), .sel({SHAMTi[1], RIGHTi}));
  Multiplexer #(.select(2)) multiplexer_30 (
    .in0(D[29]), .in1(D[29]), .in2(D[27]), .in3(D[31]), .out(Q[29]), .sel({SHAMTi[1], RIGHTi}));
  Multiplexer #(.select(2)) multiplexer_31 (
    .in0(D[30]), .in1(D[30]), .in2(D[28]), .in3(SIGNi), .out(Q[30]), .sel({SHAMTi[1], RIGHTi}));
  Multiplexer #(.select(2)) multiplexer_32 (
    .in0(D[31]), .in1(D[31]), .in2(D[29]), .in3(SIGNi), .out(Q[31]), .sel({SHAMTi[1], RIGHTi}));

  assign RIGHTo = RIGHTi;
  assign SHAMTo = SHAMTi[0];
  assign SIGNo = SIGNi;
endmodule

module EXE_ALU_BarrelShifter_Stage5 (
  input  RIGHTi,
  input  SHAMTi,
  input  [31:0] D,
  input  SIGNi,
  output [31:0] Q
);

  Multiplexer #(.select(2)) multiplexer_1 (
    .in0(D[0]), .in1(D[0]), .in2(1'b0), .in3(D[1]), .out(Q[0]), .sel({SHAMTi, RIGHTi}));
  Multiplexer #(.select(2)) multiplexer_2 (
    .in0(D[1]), .in1(D[1]), .in2(D[0]), .in3(D[2]), .out(Q[1]), .sel({SHAMTi, RIGHTi}));
  Multiplexer #(.select(2)) multiplexer_3 (
    .in0(D[2]), .in1(D[2]), .in2(D[1]), .in3(D[3]), .out(Q[2]), .sel({SHAMTi, RIGHTi}));
  Multiplexer #(.select(2)) multiplexer_4 (
    .in0(D[3]), .in1(D[3]), .in2(D[2]), .in3(D[4]), .out(Q[3]), .sel({SHAMTi, RIGHTi}));
  Multiplexer #(.select(2)) multiplexer_5 (
    .in0(D[4]), .in1(D[4]), .in2(D[3]), .in3(D[5]), .out(Q[4]), .sel({SHAMTi, RIGHTi}));
  Multiplexer #(.select(2)) multiplexer_6 (
    .in0(D[5]), .in1(D[5]), .in2(D[4]), .in3(D[6]), .out(Q[5]), .sel({SHAMTi, RIGHTi}));
  Multiplexer #(.select(2)) multiplexer_7 (
    .in0(D[6]), .in1(D[6]), .in2(D[5]), .in3(D[7]), .out(Q[6]), .sel({SHAMTi, RIGHTi}));
  Multiplexer #(.select(2)) multiplexer_8 (
    .in0(D[7]), .in1(D[7]), .in2(D[6]), .in3(D[8]), .out(Q[7]), .sel({SHAMTi, RIGHTi}));
  Multiplexer #(.select(2)) multiplexer_9 (
    .in0(D[8]), .in1(D[8]), .in2(D[7]), .in3(D[9]), .out(Q[8]), .sel({SHAMTi, RIGHTi}));
  Multiplexer #(.select(2)) multiplexer_10 (
    .in0(D[9]), .in1(D[9]), .in2(D[8]), .in3(D[10]), .out(Q[9]), .sel({SHAMTi, RIGHTi}));
  Multiplexer #(.select(2)) multiplexer_11 (
    .in0(D[10]), .in1(D[10]), .in2(D[9]), .in3(D[11]), .out(Q[10]), .sel({SHAMTi, RIGHTi}));
  Multiplexer #(.select(2)) multiplexer_12 (
    .in0(D[11]), .in1(D[11]), .in2(D[10]), .in3(D[12]), .out(Q[11]), .sel({SHAMTi, RIGHTi}));
  Multiplexer #(.select(2)) multiplexer_13 (
    .in0(D[12]), .in1(D[12]), .in2(D[11]), .in3(D[13]), .out(Q[12]), .sel({SHAMTi, RIGHTi}));
  Multiplexer #(.select(2)) multiplexer_14 (
    .in0(D[13]), .in1(D[13]), .in2(D[12]), .in3(D[14]), .out(Q[13]), .sel({SHAMTi, RIGHTi}));
  Multiplexer #(.select(2)) multiplexer_15 (
    .in0(D[14]), .in1(D[14]), .in2(D[13]), .in3(D[15]), .out(Q[14]), .sel({SHAMTi, RIGHTi}));
  Multiplexer #(.select(2)) multiplexer_16 (
    .in0(D[15]), .in1(D[15]), .in2(D[14]), .in3(D[16]), .out(Q[15]), .sel({SHAMTi, RIGHTi}));
  Multiplexer #(.select(2)) multiplexer_17 (
    .in0(D[16]), .in1(D[16]), .in2(D[15]), .in3(D[17]), .out(Q[16]), .sel({SHAMTi, RIGHTi}));
  Multiplexer #(.select(2)) multiplexer_18 (
    .in0(D[17]), .in1(D[17]), .in2(D[16]), .in3(D[18]), .out(Q[17]), .sel({SHAMTi, RIGHTi}));
  Multiplexer #(.select(2)) multiplexer_19 (
    .in0(D[18]), .in1(D[18]), .in2(D[17]), .in3(D[19]), .out(Q[18]), .sel({SHAMTi, RIGHTi}));
  Multiplexer #(.select(2)) multiplexer_20 (
    .in0(D[19]), .in1(D[19]), .in2(D[18]), .in3(D[20]), .out(Q[19]), .sel({SHAMTi, RIGHTi}));
  Multiplexer #(.select(2)) multiplexer_21 (
    .in0(D[20]), .in1(D[20]), .in2(D[19]), .in3(D[21]), .out(Q[20]), .sel({SHAMTi, RIGHTi}));
  Multiplexer #(.select(2)) multiplexer_22 (
    .in0(D[21]), .in1(D[21]), .in2(D[20]), .in3(D[22]), .out(Q[21]), .sel({SHAMTi, RIGHTi}));
  Multiplexer #(.select(2)) multiplexer_23 (
    .in0(D[22]), .in1(D[22]), .in2(D[21]), .in3(D[23]), .out(Q[22]), .sel({SHAMTi, RIGHTi}));
  Multiplexer #(.select(2)) multiplexer_24 (
    .in0(D[23]), .in1(D[23]), .in2(D[22]), .in3(D[24]), .out(Q[23]), .sel({SHAMTi, RIGHTi}));
  Multiplexer #(.select(2)) multiplexer_25 (
    .in0(D[24]), .in1(D[24]), .in2(D[23]), .in3(D[25]), .out(Q[24]), .sel({SHAMTi, RIGHTi}));
  Multiplexer #(.select(2)) multiplexer_26 (
    .in0(D[25]), .in1(D[25]), .in2(D[24]), .in3(D[26]), .out(Q[25]), .sel({SHAMTi, RIGHTi}));
  Multiplexer #(.select(2)) multiplexer_27 (
    .in0(D[26]), .in1(D[26]), .in2(D[25]), .in3(D[27]), .out(Q[26]), .sel({SHAMTi, RIGHTi}));
  Multiplexer #(.select(2)) multiplexer_28 (
    .in0(D[27]), .in1(D[27]), .in2(D[26]), .in3(D[28]), .out(Q[27]), .sel({SHAMTi, RIGHTi}));
  Multiplexer #(.select(2)) multiplexer_29 (
    .in0(D[28]), .in1(D[28]), .in2(D[27]), .in3(D[29]), .out(Q[28]), .sel({SHAMTi, RIGHTi}));
  Multiplexer #(.select(2)) multiplexer_30 (
    .in0(D[29]), .in1(D[29]), .in2(D[28]), .in3(D[30]), .out(Q[29]), .sel({SHAMTi, RIGHTi}));
  Multiplexer #(.select(2)) multiplexer_31 (
    .in0(D[30]), .in1(D[30]), .in2(D[29]), .in3(D[31]), .out(Q[30]), .sel({SHAMTi, RIGHTi}));
  Multiplexer #(.select(2)) multiplexer_32 (
    .in0(D[31]), .in1(D[31]), .in2(D[30]), .in3(SIGNi), .out(Q[31]), .sel({SHAMTi, RIGHTi}));
endmodule

module EXE_ALU_Adder (
  input  CLK,
  input  [31:0] S1,
  input  [31:0] S2,
  input  SUB
);

  wire register_3_q, Stage1_subo, Stage2_co;
  wire [7:0] Stage2_q;
  wire [23:0] Stage2_s1o, Stage2_s2o;
  wire [31:0] register_1_q, register_2_q, Stage1_s1o, Stage1_s2o;

  EXE_ALU_Adder_Stage1 Stage1 (.S1i(S1), .S2i(S2), .SUBi(SUB), .S1o(Stage1_s1o), .S2o(Stage1_s2o), .SUBo(Stage1_subo));
  Register #(.width(32)) register_1 (.D(Stage1_s1o), .en(1'b1), .clk(CLK), .Q(register_1_q), .clr(1'b0));
  Register #(.width(32)) register_2 (.D(Stage1_s2o), .en(1'b1), .clk(CLK), .Q(register_2_q), .clr(1'b0));
  Register #(.width(1)) register_3 (.D(Stage1_subo), .en(1'b1), .clk(CLK), .Q(register_3_q), .clr(1'b0));
  EXE_ALU_Adder_Stage2 Stage2 (
    .S1i(register_1_q), .S2i(register_2_q), .SUBi(register_3_q), .Q(Stage2_q), .S1o(Stage2_s1o),
    .S2o(Stage2_s2o), .Co(Stage2_co));
  Register register_4 (.D(Stage2_q), .en(1'b1), .clk(CLK), .clr(1'b0));  // open: Q
  Register #(.width(24)) register_5 (.D(Stage2_s1o), .en(1'b1), .clk(CLK), .clr(1'b0));  // open: Q
  Register #(.width(24)) register_6 (.D(Stage2_s2o), .en(1'b1), .clk(CLK), .clr(1'b0));  // open: Q
  Register #(.width(1)) register_7 (.D(Stage2_co), .en(1'b1), .clk(CLK), .clr(1'b0));  // open: Q
endmodule

module EXE_ALU_Adder_Stage1 (
  input  [31:0] S1i,
  input  [31:0] S2i,
  input  SUBi,
  output [31:0] S1o,
  output [31:0] S2o,
  output SUBo
);

  xor xor_1 (S2o[0], S2i[0], SUBi);
  xor xor_2 (S2o[1], S2i[1], SUBi);
  xor xor_3 (S2o[2], S2i[2], SUBi);
  xor xor_4 (S2o[3], S2i[3], SUBi);
  xor xor_5 (S2o[4], S2i[4], SUBi);
  xor xor_6 (S2o[5], S2i[5], SUBi);
  xor xor_7 (S2o[6], S2i[6], SUBi);
  xor xor_8 (S2o[7], S2i[7], SUBi);
  xor xor_9 (S2o[8], S2i[8], SUBi);
  xor xor_10 (S2o[9], S2i[9], SUBi);
  xor xor_11 (S2o[10], S2i[10], SUBi);
  xor xor_12 (S2o[11], S2i[11], SUBi);
  xor xor_13 (S2o[12], S2i[12], SUBi);
  xor xor_14 (S2o[13], S2i[13], SUBi);
  xor xor_15 (S2o[14], S2i[14], SUBi);
  xor xor_16 (S2o[15], S2i[15], SUBi);
  xor xor_17 (S2o[16], S2i[16], SUBi);
  xor xor_18 (S2o[17], S2i[17], SUBi);
  xor xor_19 (S2o[18], S2i[18], SUBi);
  xor xor_20 (S2o[19], S2i[19], SUBi);
  xor xor_21 (S2o[20], S2i[20], SUBi);
  xor xor_22 (S2o[21], S2i[21], SUBi);
  xor xor_23 (S2o[22], S2i[22], SUBi);
  xor xor_24 (S2o[23], S2i[23], SUBi);
  xor xor_25 (S2o[24], S2i[24], SUBi);
  xor xor_26 (S2o[25], S2i[25], SUBi);
  xor xor_27 (S2o[26], S2i[26], SUBi);
  xor xor_28 (S2o[27], S2i[27], SUBi);
  xor xor_29 (S2o[28], S2i[28], SUBi);
  xor xor_30 (S2o[29], S2i[29], SUBi);
  xor xor_31 (S2o[30], S2i[30], SUBi);
  xor xor_32 (S2o[31], S2i[31], SUBi);

  assign S1o = S1i;
  assign SUBo = SUBi;
endmodule

module EXE_ALU_Adder_Stage2 (
  input  [31:0] S1i,
  input  [31:0] S2i,
  input  SUBi,
  output [7:0] Q,
  output [23:0] S1o,
  output [23:0] S2o,
  output Co
);

  wire adder_1_cout;

  Adder #(.width(4)) adder_1 (.a(S1i[3:0]), .b(S2i[3:0]), .out(Q[3:0]), .cin(SUBi), .cout(adder_1_cout));
  Adder #(.width(4)) adder_2 (.a(S1i[7:4]), .b(S2i[7:4]), .out(Q[7:4]), .cin(adder_1_cout), .cout(Co));

  assign S1o = S1i[31:8];
  assign S2o = S2i[31:8];
endmodule
