// Logisim project RV.circ as structural Verilog: 13 circuits, main circuit main
module main (
  input  RESET
);

  wire CLK_out, decode_ctrl_1_alu_sel, decode_ctrl_1_branch, decode_ctrl_1_jump, decode_ctrl_1_mem_write,
       decode_ctrl_1_reg_write, execute_ctrl_1_alu_selo, execute_ctrl_1_mem_writeo, execute_ctrl_1_pc_src,
       execute_ctrl_1_reg_writeo, execute_data_1_zero, mem_ctrl_1_mem_writeo, mem_ctrl_1_reg_writeo,
       wb_ctrl_1_reg_writeo;
  wire [1:0] decode_ctrl_1_imm_sel, decode_ctrl_1_result_sel, execute_ctrl_1_result_selo,
       mem_ctrl_1_result_selo, wb_ctrl_1_result_selo;
  wire [2:0] decode_ctrl_1_alu_func, execute_ctrl_1_alu_funco;
  wire [4:0] decode_ctrl_1_ad, decode_ctrl_1_as1, decode_ctrl_1_as2, execute_ctrl_1_ado, mem_ctrl_1_ado,
       wb_ctrl_1_ado;
  wire [31:0] decode_ctrl_1_imm_src, decode_data_1_imm, decode_data_1_pc4o, decode_data_1_pco,
       decode_data_1_s1, decode_data_1_s2, execute_data_1_alu_result, execute_data_1_pc4o,
       execute_data_1_target, execute_data_1_wd, fetch_ctrl_1_instr, fetch_ctrl_1_pc, fetch_ctrl_1_pc4,
       mem_data_1_alu_resulto, mem_data_1_pc4o, mem_data_1_rd, wb_data_1_result;

  Clock CLK (.out(CLK_out));
  fetch_ctrl fetch_ctrl_1 (
    .PC_SRC(execute_ctrl_1_pc_src), .TARGET(execute_data_1_target), .CLK(CLK_out), .RESET(RESET),
    .INSTR(fetch_ctrl_1_instr), .PC(fetch_ctrl_1_pc), .PC4(fetch_ctrl_1_pc4));  // open: STALL
  // Probe on fetch_ctrl_1_pc
  // Probe on fetch_ctrl_1_pc4
  // Probe on fetch_ctrl_1_instr
  decode_ctrl decode_ctrl_1 (
    .INSTR(fetch_ctrl_1_instr), .CLK(CLK_out), .RESET(RESET), .REG_WRITE(decode_ctrl_1_reg_write),
    .RESULT_SEL(decode_ctrl_1_result_sel), .MEM_WRITE(decode_ctrl_1_mem_write), .JUMP(decode_ctrl_1_jump),
    .BRANCH(decode_ctrl_1_branch), .ALU_FUNC(decode_ctrl_1_alu_func), .ALU_SEL(decode_ctrl_1_alu_sel),
    .AS1(decode_ctrl_1_as1), .AS2(decode_ctrl_1_as2), .AD(decode_ctrl_1_ad), .IMM_SEL(decode_ctrl_1_imm_sel),
    .IMM_SRC(decode_ctrl_1_imm_src));  // open: STALL, FLUSH
  decode_data decode_data_1 (
    .AS1(decode_ctrl_1_as2), .AS2(decode_ctrl_1_ad), .IMM_SEL(decode_ctrl_1_imm_sel),
    .IMM_SRC(decode_ctrl_1_imm_src), .PC(fetch_ctrl_1_pc), .PC4(fetch_ctrl_1_pc4), .CLK(CLK_out),
    .RESET(RESET), .REG_WRITE(wb_ctrl_1_reg_writeo), .RESULT(wb_data_1_result), .AD(wb_ctrl_1_ado),
    .IMM(decode_data_1_imm), .S1(decode_data_1_s1), .S2(decode_data_1_s2), .PCo(decode_data_1_pco),
    .PC4o(decode_data_1_pc4o));  // open: STALL, FLUSH
  execute_ctrl execute_ctrl_1 (
    .REG_WRITE(decode_ctrl_1_reg_write), .RESULT_SEL(decode_ctrl_1_result_sel),
    .MEM_WRITE(decode_ctrl_1_mem_write), .JUMP(decode_ctrl_1_jump), .BRANCH(decode_ctrl_1_branch),
    .ALU_FUNC(decode_ctrl_1_alu_func), .ALU_SEL(decode_ctrl_1_alu_sel), .AS1(decode_ctrl_1_as1),
    .AS2(decode_ctrl_1_as2), .AD(decode_ctrl_1_ad), .CLK(CLK_out), .RESET(RESET), .ZERO(execute_data_1_zero),
    .REG_WRITEo(execute_ctrl_1_reg_writeo), .RESULT_SELo(execute_ctrl_1_result_selo),
    .MEM_WRITEo(execute_ctrl_1_mem_writeo), .ALU_FUNCo(execute_ctrl_1_alu_funco),
    .ALU_SELo(execute_ctrl_1_alu_selo), .ADo(execute_ctrl_1_ado), .PC_SRC(execute_ctrl_1_pc_src));  // open: FLUSH, AS1o, AS2o
  execute_data execute_data_1 (
    .ALU_FUNC(execute_ctrl_1_alu_funco), .ALU_SEL(execute_ctrl_1_alu_selo), .IMM(decode_data_1_imm),
    .S1(decode_data_1_s1), .S2(decode_data_1_s2), .PC4(decode_data_1_pco), .PC(decode_data_1_pc4o),
    .CLK(CLK_out), .RESET(RESET), .ZERO(execute_data_1_zero), .ALU_RESULT(execute_data_1_alu_result),
    .WD(execute_data_1_wd), .PC4o(execute_data_1_pc4o), .TARGET(execute_data_1_target));  // open: FLUSH
  mem_ctrl mem_ctrl_1 (
    .REG_WRITE(execute_ctrl_1_reg_writeo), .RESULT_SEL(execute_ctrl_1_result_selo),
    .MEM_WRITE(execute_ctrl_1_mem_writeo), .AD(execute_ctrl_1_ado), .CLK(CLK_out), .RESET(RESET),
    .REG_WRITEo(mem_ctrl_1_reg_writeo), .RESULT_SELo(mem_ctrl_1_result_selo),
    .MEM_WRITEo(mem_ctrl_1_mem_writeo), .ADo(mem_ctrl_1_ado));
  mem_data mem_data_1 (
    .MEM_WRITE(mem_ctrl_1_mem_writeo), .ALU_RESULT(execute_data_1_alu_result), .WD(execute_data_1_wd),
    .PC4(execute_data_1_pc4o), .CLK(CLK_out), .RESET(RESET), .ALU_RESULTo(mem_data_1_alu_resulto),
    .RD(mem_data_1_rd), .PC4o(mem_data_1_pc4o));
  wb_ctrl wb_ctrl_1 (
    .REG_WRITE(mem_ctrl_1_reg_writeo), .RESULT_SEL(mem_ctrl_1_result_selo), .AD(mem_ctrl_1_ado),
    .CLK(CLK_out), .RESET(RESET), .REG_WRITEo(wb_ctrl_1_reg_writeo), .RESULT_SELo(wb_ctrl_1_result_selo),
    .ADo(wb_ctrl_1_ado));
  wb_data wb_data_1 (
    .RESULT_SEL(wb_ctrl_1_result_selo), .ALU_RESULT(mem_data_1_alu_resulto), .RD(mem_data_1_rd),
    .PC4(mem_data_1_pc4o), .CLK(CLK_out), .RESET(RESET), .RESULT(wb_data_1_result));
endmodule

module fetch_ctrl (
  input  PC_SRC,
  input  [31:0] TARGET,
  input  STALL,
  input  CLK,
  input  RESET,
  output [31:0] INSTR,
  output [31:0] PC,
  output [31:0] PC4
);

  wire not_1_out;
  wire [31:0] multiplexer_1_out;

  Multiplexer #(.width(32)) multiplexer_1 (.in0(TARGET), .in1(PC4), .out(multiplexer_1_out), .sel(PC_SRC));
  not not_1 (not_1_out, STALL);
  Register #(.width(32)) PC_REG (.D(multiplexer_1_out), .en(not_1_out), .clk(CLK), .Q(PC), .clr(RESET));
  Adder #(.width(32)) adder_1 (.a(PC), .b(32'h4), .out(PC4));  // open: cin, cout
  ROM #(.addrWidth(16), .dataWidth(32)) IMEM (.addr(PC[17:2]), .data(INSTR));

  // Notes on the sheet:
  //   contents of IMEM (hex, n*v repeats v):
  //   3e800093 7d008113 c1810193 83018213 3e820293
endmodule

module decode_ctrl (
  input  [31:0] INSTR,
  input  STALL,
  input  FLUSH,
  input  CLK,
  input  RESET,
  output REG_WRITE,
  output [1:0] RESULT_SEL,
  output MEM_WRITE,
  output JUMP,
  output BRANCH,
  output [2:0] ALU_FUNC,
  output ALU_SEL,
  output [4:0] AS1,
  output [4:0] AS2,
  output [4:0] AD,
  output [1:0] IMM_SEL,
  output [31:0] IMM_SRC
);

  wire not_1_out, or_1_out;
  wire [8:6] pla_1_out;

  Register #(.width(32)) register_1 (
    .D(INSTR), .en(not_1_out), .clk(CLK), .Q({IMM_SRC[31:25], AS2, AS1, IMM_SRC[14:12], AD, IMM_SRC[6:0]}),
    .clr(or_1_out));
  not not_1 (not_1_out, STALL);
  or or_1 (or_1_out, FLUSH, RESET);
  PLA #(.in_width(5), .out_width(10), .\table ("00100 1000000001")) pla_1 (
    .in(IMM_SRC[6:2]), .out({ALU_SEL, pla_1_out, BRANCH, JUMP, MEM_WRITE, RESULT_SEL, REG_WRITE}));
  PLA #(.in_width(5), .\table ("00000 00")) pla_2 (.in(IMM_SRC[6:2]), .out(IMM_SEL));

  assign {IMM_SRC[24:15], IMM_SRC[11:7]} = {AS2, AS1, AD};
endmodule

module decode_data (
  input  [4:0] AS1,
  input  [4:0] AS2,
  input  [1:0] IMM_SEL,
  input  [31:0] IMM_SRC,
  input  [31:0] PC,
  input  [31:0] PC4,
  input  STALL,
  input  FLUSH,
  input  CLK,
  input  RESET,
  input  REG_WRITE,
  input  [31:0] RESULT,
  input  [4:0] AD,
  output [31:0] IMM,
  output [31:0] S1,
  output [31:0] S2,
  output [31:0] PCo,
  output [31:0] PC4o
);

  wire not_1_out, or_1_out;

  not not_1 (not_1_out, STALL);
  Register #(.width(32)) register_1 (.D(PC), .en(not_1_out), .clk(CLK), .Q(PCo), .clr(or_1_out));
  Register #(.width(32)) register_2 (.D(PC4), .en(not_1_out), .clk(CLK), .Q(PC4o), .clr(or_1_out));
  or or_1 (or_1_out, FLUSH, RESET);
  extender extender_1 (.IMM_SEL(IMM_SEL), .IMM_SRC(IMM_SRC), .IMM(IMM));
  register_file register_file_1 (
    .CLK(CLK), .RESET(RESET), .AS1(AS1), .AS2(AS2), .AD(AD), .WE(REG_WRITE), .D(RESULT), .S1(S1), .S2(S2));
endmodule

module register_file (
  input  CLK,
  input  RESET,
  input  [4:0] AS1,
  input  [4:0] AS2,
  input  [4:0] AD,
  input  WE,
  input  [31:0] D,
  output [31:0] S1,
  output [31:0] S2
);

  wire [31:0] decoder_1_out0, decoder_2_out0, decoder_3_out0, register_1_q, register_2_q, register_3_q,
       register_4_q, register_5_q, register_6_q, register_7_q, register_8_q, register_9_q, register_10_q,
       register_11_q, register_12_q, register_13_q, register_14_q, register_15_q, register_16_q,
       register_17_q, register_18_q, register_19_q, register_20_q, register_21_q, register_22_q,
       register_23_q, register_24_q, register_25_q, register_26_q, register_27_q, register_28_q,
       register_29_q, register_30_q, register_31_q;

  Decoder #(.enable("false"), .select(5)) decoder_1 (
    .out0(decoder_1_out0[0]), .out1(decoder_1_out0[1]), .out2(decoder_1_out0[2]), .out3(decoder_1_out0[3]),
    .out4(decoder_1_out0[4]), .out5(decoder_1_out0[5]), .out6(decoder_1_out0[6]), .out7(decoder_1_out0[7]),
    .out8(decoder_1_out0[8]), .out9(decoder_1_out0[9]), .out10(decoder_1_out0[10]),
    .out11(decoder_1_out0[11]), .out12(decoder_1_out0[12]), .out13(decoder_1_out0[13]),
    .out14(decoder_1_out0[14]), .out15(decoder_1_out0[15]), .out16(decoder_1_out0[16]),
    .out17(decoder_1_out0[17]), .out18(decoder_1_out0[18]), .out19(decoder_1_out0[19]),
    .out20(decoder_1_out0[20]), .out21(decoder_1_out0[21]), .out22(decoder_1_out0[22]),
    .out23(decoder_1_out0[23]), .out24(decoder_1_out0[24]), .out25(decoder_1_out0[25]),
    .out26(decoder_1_out0[26]), .out27(decoder_1_out0[27]), .out28(decoder_1_out0[28]),
    .out29(decoder_1_out0[29]), .out30(decoder_1_out0[30]), .out31(decoder_1_out0[31]), .sel(AS1));
  Decoder #(.enable("false"), .select(5)) decoder_2 (
    .out0(decoder_2_out0[0]), .out1(decoder_2_out0[1]), .out2(decoder_2_out0[2]), .out3(decoder_2_out0[3]),
    .out4(decoder_2_out0[4]), .out5(decoder_2_out0[5]), .out6(decoder_2_out0[6]), .out7(decoder_2_out0[7]),
    .out8(decoder_2_out0[8]), .out9(decoder_2_out0[9]), .out10(decoder_2_out0[10]),
    .out11(decoder_2_out0[11]), .out12(decoder_2_out0[12]), .out13(decoder_2_out0[13]),
    .out14(decoder_2_out0[14]), .out15(decoder_2_out0[15]), .out16(decoder_2_out0[16]),
    .out17(decoder_2_out0[17]), .out18(decoder_2_out0[18]), .out19(decoder_2_out0[19]),
    .out20(decoder_2_out0[20]), .out21(decoder_2_out0[21]), .out22(decoder_2_out0[22]),
    .out23(decoder_2_out0[23]), .out24(decoder_2_out0[24]), .out25(decoder_2_out0[25]),
    .out26(decoder_2_out0[26]), .out27(decoder_2_out0[27]), .out28(decoder_2_out0[28]),
    .out29(decoder_2_out0[29]), .out30(decoder_2_out0[30]), .out31(decoder_2_out0[31]), .sel(AS2));
  Decoder #(.select(5)) decoder_3 (
    .out0(decoder_3_out0[0]), .out1(decoder_3_out0[1]), .out2(decoder_3_out0[2]), .out3(decoder_3_out0[3]),
    .out4(decoder_3_out0[4]), .out5(decoder_3_out0[5]), .out6(decoder_3_out0[6]), .out7(decoder_3_out0[7]),
    .out8(decoder_3_out0[8]), .out9(decoder_3_out0[9]), .out10(decoder_3_out0[10]),
    .out11(decoder_3_out0[11]), .out12(decoder_3_out0[12]), .out13(decoder_3_out0[13]),
    .out14(decoder_3_out0[14]), .out15(decoder_3_out0[15]), .out16(decoder_3_out0[16]),
    .out17(decoder_3_out0[17]), .out18(decoder_3_out0[18]), .out19(decoder_3_out0[19]),
    .out20(decoder_3_out0[20]), .out21(decoder_3_out0[21]), .out22(decoder_3_out0[22]),
    .out23(decoder_3_out0[23]), .out24(decoder_3_out0[24]), .out25(decoder_3_out0[25]),
    .out26(decoder_3_out0[26]), .out27(decoder_3_out0[27]), .out28(decoder_3_out0[28]),
    .out29(decoder_3_out0[29]), .out30(decoder_3_out0[30]), .out31(decoder_3_out0[31]), .sel(AD), .en(WE));
  Register #(.width(32)) register_1 (.D(D), .en(decoder_3_out0[1]), .clk(CLK), .Q(register_1_q), .clr(RESET));
  Register #(.width(32)) register_2 (.D(D), .en(decoder_3_out0[2]), .clk(CLK), .Q(register_2_q), .clr(RESET));
  Register #(.width(32)) register_3 (.D(D), .en(decoder_3_out0[3]), .clk(CLK), .Q(register_3_q), .clr(RESET));
  Register #(.width(32)) register_4 (.D(D), .en(decoder_3_out0[4]), .clk(CLK), .Q(register_4_q), .clr(RESET));
  Register #(.width(32)) register_5 (.D(D), .en(decoder_3_out0[5]), .clk(CLK), .Q(register_5_q), .clr(RESET));
  Register #(.width(32)) register_6 (.D(D), .en(decoder_3_out0[6]), .clk(CLK), .Q(register_6_q), .clr(RESET));
  Register #(.width(32)) register_7 (.D(D), .en(decoder_3_out0[7]), .clk(CLK), .Q(register_7_q), .clr(RESET));
  assign S1 = decoder_1_out0[0] ? {32{1'b0}} : 32'bz;  // Controlled_Buffer controlled_buffer_1
  assign S2 = decoder_2_out0[0] ? {32{1'b0}} : 32'bz;  // Controlled_Buffer controlled_buffer_2
  assign S1 = decoder_1_out0[1] ? register_1_q : 32'bz;  // Controlled_Buffer controlled_buffer_3
  assign S2 = decoder_2_out0[1] ? register_1_q : 32'bz;  // Controlled_Buffer controlled_buffer_4
  assign S1 = decoder_1_out0[2] ? register_2_q : 32'bz;  // Controlled_Buffer controlled_buffer_5
  assign S2 = decoder_2_out0[2] ? register_2_q : 32'bz;  // Controlled_Buffer controlled_buffer_6
  assign S1 = decoder_1_out0[3] ? register_3_q : 32'bz;  // Controlled_Buffer controlled_buffer_7
  assign S2 = decoder_2_out0[3] ? register_3_q : 32'bz;  // Controlled_Buffer controlled_buffer_8
  assign S1 = decoder_1_out0[4] ? register_4_q : 32'bz;  // Controlled_Buffer controlled_buffer_9
  assign S2 = decoder_2_out0[4] ? register_4_q : 32'bz;  // Controlled_Buffer controlled_buffer_10
  assign S1 = decoder_1_out0[5] ? register_5_q : 32'bz;  // Controlled_Buffer controlled_buffer_11
  assign S2 = decoder_2_out0[5] ? register_5_q : 32'bz;  // Controlled_Buffer controlled_buffer_12
  assign S1 = decoder_1_out0[6] ? register_6_q : 32'bz;  // Controlled_Buffer controlled_buffer_13
  assign S2 = decoder_2_out0[6] ? register_6_q : 32'bz;  // Controlled_Buffer controlled_buffer_14
  assign S1 = decoder_1_out0[7] ? register_7_q : 32'bz;  // Controlled_Buffer controlled_buffer_15
  assign S2 = decoder_2_out0[7] ? register_7_q : 32'bz;  // Controlled_Buffer controlled_buffer_16
  Register #(.width(32)) register_8 (.D(D), .en(decoder_3_out0[8]), .clk(CLK), .Q(register_8_q), .clr(RESET));
  Register #(.width(32)) register_9 (.D(D), .en(decoder_3_out0[9]), .clk(CLK), .Q(register_9_q), .clr(RESET));
  Register #(.width(32)) register_10 (.D(D), .en(decoder_3_out0[10]), .clk(CLK), .Q(register_10_q), .clr(RESET));
  Register #(.width(32)) register_11 (.D(D), .en(decoder_3_out0[11]), .clk(CLK), .Q(register_11_q), .clr(RESET));
  Register #(.width(32)) register_12 (.D(D), .en(decoder_3_out0[12]), .clk(CLK), .Q(register_12_q), .clr(RESET));
  Register #(.width(32)) register_13 (.D(D), .en(decoder_3_out0[13]), .clk(CLK), .Q(register_13_q), .clr(RESET));
  Register #(.width(32)) register_14 (.D(D), .en(decoder_3_out0[14]), .clk(CLK), .Q(register_14_q), .clr(RESET));
  Register #(.width(32)) register_15 (.D(D), .en(decoder_3_out0[15]), .clk(CLK), .Q(register_15_q), .clr(RESET));
  assign S1 = decoder_1_out0[8] ? register_8_q : 32'bz;  // Controlled_Buffer controlled_buffer_17
  assign S2 = decoder_2_out0[8] ? register_8_q : 32'bz;  // Controlled_Buffer controlled_buffer_18
  assign S1 = decoder_1_out0[9] ? register_9_q : 32'bz;  // Controlled_Buffer controlled_buffer_19
  assign S2 = decoder_2_out0[9] ? register_9_q : 32'bz;  // Controlled_Buffer controlled_buffer_20
  assign S1 = decoder_1_out0[10] ? register_10_q : 32'bz;  // Controlled_Buffer controlled_buffer_21
  assign S2 = decoder_2_out0[10] ? register_10_q : 32'bz;  // Controlled_Buffer controlled_buffer_22
  assign S1 = decoder_1_out0[11] ? register_11_q : 32'bz;  // Controlled_Buffer controlled_buffer_23
  assign S2 = decoder_2_out0[11] ? register_11_q : 32'bz;  // Controlled_Buffer controlled_buffer_24
  assign S1 = decoder_1_out0[12] ? register_12_q : 32'bz;  // Controlled_Buffer controlled_buffer_25
  assign S2 = decoder_2_out0[12] ? register_12_q : 32'bz;  // Controlled_Buffer controlled_buffer_26
  assign S1 = decoder_1_out0[13] ? register_13_q : 32'bz;  // Controlled_Buffer controlled_buffer_27
  assign S2 = decoder_2_out0[13] ? register_13_q : 32'bz;  // Controlled_Buffer controlled_buffer_28
  assign S1 = decoder_1_out0[14] ? register_14_q : 32'bz;  // Controlled_Buffer controlled_buffer_29
  assign S2 = decoder_2_out0[14] ? register_14_q : 32'bz;  // Controlled_Buffer controlled_buffer_30
  assign S1 = decoder_1_out0[15] ? register_15_q : 32'bz;  // Controlled_Buffer controlled_buffer_31
  assign S2 = decoder_2_out0[15] ? register_15_q : 32'bz;  // Controlled_Buffer controlled_buffer_32
  Register #(.width(32)) register_16 (.D(D), .en(decoder_3_out0[16]), .clk(CLK), .Q(register_16_q), .clr(RESET));
  Register #(.width(32)) register_17 (.D(D), .en(decoder_3_out0[17]), .clk(CLK), .Q(register_17_q), .clr(RESET));
  Register #(.width(32)) register_18 (.D(D), .en(decoder_3_out0[18]), .clk(CLK), .Q(register_18_q), .clr(RESET));
  Register #(.width(32)) register_19 (.D(D), .en(decoder_3_out0[19]), .clk(CLK), .Q(register_19_q), .clr(RESET));
  Register #(.width(32)) register_20 (.D(D), .en(decoder_3_out0[20]), .clk(CLK), .Q(register_20_q), .clr(RESET));
  Register #(.width(32)) register_21 (.D(D), .en(decoder_3_out0[21]), .clk(CLK), .Q(register_21_q), .clr(RESET));
  Register #(.width(32)) register_22 (.D(D), .en(decoder_3_out0[22]), .clk(CLK), .Q(register_22_q), .clr(RESET));
  Register #(.width(32)) register_23 (.D(D), .en(decoder_3_out0[23]), .clk(CLK), .Q(register_23_q), .clr(RESET));
  assign S1 = decoder_1_out0[16] ? register_16_q : 32'bz;  // Controlled_Buffer controlled_buffer_33
  assign S2 = decoder_2_out0[16] ? register_16_q : 32'bz;  // Controlled_Buffer controlled_buffer_34
  assign S1 = decoder_1_out0[17] ? register_17_q : 32'bz;  // Controlled_Buffer controlled_buffer_35
  assign S2 = decoder_2_out0[17] ? register_17_q : 32'bz;  // Controlled_Buffer controlled_buffer_36
  assign S1 = decoder_1_out0[18] ? register_18_q : 32'bz;  // Controlled_Buffer controlled_buffer_37
  assign S2 = decoder_2_out0[18] ? register_18_q : 32'bz;  // Controlled_Buffer controlled_buffer_38
  assign S1 = decoder_1_out0[19] ? register_19_q : 32'bz;  // Controlled_Buffer controlled_buffer_39
  assign S2 = decoder_2_out0[19] ? register_19_q : 32'bz;  // Controlled_Buffer controlled_buffer_40
  assign S1 = decoder_1_out0[20] ? register_20_q : 32'bz;  // Controlled_Buffer controlled_buffer_41
  assign S2 = decoder_2_out0[20] ? register_20_q : 32'bz;  // Controlled_Buffer controlled_buffer_42
  assign S1 = decoder_1_out0[21] ? register_21_q : 32'bz;  // Controlled_Buffer controlled_buffer_43
  assign S2 = decoder_2_out0[21] ? register_21_q : 32'bz;  // Controlled_Buffer controlled_buffer_44
  assign S1 = decoder_1_out0[22] ? register_22_q : 32'bz;  // Controlled_Buffer controlled_buffer_45
  assign S2 = decoder_2_out0[22] ? register_22_q : 32'bz;  // Controlled_Buffer controlled_buffer_46
  assign S1 = decoder_1_out0[23] ? register_23_q : 32'bz;  // Controlled_Buffer controlled_buffer_47
  assign S2 = decoder_2_out0[23] ? register_23_q : 32'bz;  // Controlled_Buffer controlled_buffer_48
  Register #(.width(32)) register_24 (.D(D), .en(decoder_3_out0[24]), .clk(CLK), .Q(register_24_q), .clr(RESET));
  Register #(.width(32)) register_25 (.D(D), .en(decoder_3_out0[25]), .clk(CLK), .Q(register_25_q), .clr(RESET));
  Register #(.width(32)) register_26 (.D(D), .en(decoder_3_out0[26]), .clk(CLK), .Q(register_26_q), .clr(RESET));
  Register #(.width(32)) register_27 (.D(D), .en(decoder_3_out0[27]), .clk(CLK), .Q(register_27_q), .clr(RESET));
  Register #(.width(32)) register_28 (.D(D), .en(decoder_3_out0[28]), .clk(CLK), .Q(register_28_q), .clr(RESET));
  Register #(.width(32)) register_29 (.D(D), .en(decoder_3_out0[29]), .clk(CLK), .Q(register_29_q), .clr(RESET));
  Register #(.width(32)) register_30 (.D(D), .en(decoder_3_out0[30]), .clk(CLK), .Q(register_30_q), .clr(RESET));
  Register #(.width(32)) register_31 (.D(D), .en(decoder_3_out0[31]), .clk(CLK), .Q(register_31_q), .clr(RESET));
  assign S1 = decoder_1_out0[24] ? register_24_q : 32'bz;  // Controlled_Buffer controlled_buffer_49
  assign S2 = decoder_2_out0[24] ? register_24_q : 32'bz;  // Controlled_Buffer controlled_buffer_50
  assign S1 = decoder_1_out0[25] ? register_25_q : 32'bz;  // Controlled_Buffer controlled_buffer_51
  assign S2 = decoder_2_out0[25] ? register_25_q : 32'bz;  // Controlled_Buffer controlled_buffer_52
  assign S1 = decoder_1_out0[26] ? register_26_q : 32'bz;  // Controlled_Buffer controlled_buffer_53
  assign S2 = decoder_2_out0[26] ? register_26_q : 32'bz;  // Controlled_Buffer controlled_buffer_54
  assign S1 = decoder_1_out0[27] ? register_27_q : 32'bz;  // Controlled_Buffer controlled_buffer_55
  assign S2 = decoder_2_out0[27] ? register_27_q : 32'bz;  // Controlled_Buffer controlled_buffer_56
  assign S1 = decoder_1_out0[28] ? register_28_q : 32'bz;  // Controlled_Buffer controlled_buffer_57
  assign S2 = decoder_2_out0[28] ? register_28_q : 32'bz;  // Controlled_Buffer controlled_buffer_58
  assign S1 = decoder_1_out0[29] ? register_29_q : 32'bz;  // Controlled_Buffer controlled_buffer_59
  assign S2 = decoder_2_out0[29] ? register_29_q : 32'bz;  // Controlled_Buffer controlled_buffer_60
  assign S1 = decoder_1_out0[30] ? register_30_q : 32'bz;  // Controlled_Buffer controlled_buffer_61
  assign S2 = decoder_2_out0[30] ? register_30_q : 32'bz;  // Controlled_Buffer controlled_buffer_62
  assign S1 = decoder_1_out0[31] ? register_31_q : 32'bz;  // Controlled_Buffer controlled_buffer_63
  assign S2 = decoder_2_out0[31] ? register_31_q : 32'bz;  // Controlled_Buffer controlled_buffer_64
endmodule

module extender (
  input  [1:0] IMM_SEL,
  input  [31:0] IMM_SRC,
  output [31:0] IMM
);

  wire [31:0] bit_extender_1_out, bit_extender_2_out, bit_extender_3_out, bit_extender_4_out;

  assign bit_extender_1_out = {{20{IMM_SRC[31]}}, IMM_SRC[31:20]};  // Bit_Extender bit_extender_1
  assign bit_extender_2_out = {{20{IMM_SRC[31]}}, {IMM_SRC[31:25], IMM_SRC[11:7]}};  // Bit_Extender bit_extender_2
  assign bit_extender_3_out = {{19{IMM_SRC[31]}}, {IMM_SRC[31], IMM_SRC[7], IMM_SRC[30:25], IMM_SRC[11:8], 1'b0}};  // Bit_Extender bit_extender_3
  assign bit_extender_4_out = {{11{IMM_SRC[31]}}, {IMM_SRC[31], IMM_SRC[19:12], IMM_SRC[20], IMM_SRC[30:21], 1'b0}};  // Bit_Extender bit_extender_4
  Multiplexer #(.select(2), .width(32)) multiplexer_1 (
    .in0(bit_extender_1_out), .in1(bit_extender_2_out), .in2(bit_extender_3_out), .in3(bit_extender_4_out),
    .out(IMM), .sel(IMM_SEL));
endmodule

module execute_ctrl (
  input  REG_WRITE,
  input  [1:0] RESULT_SEL,
  input  MEM_WRITE,
  input  JUMP,
  input  BRANCH,
  input  [2:0] ALU_FUNC,
  input  ALU_SEL,
  input  [4:0] AS1,
  input  [4:0] AS2,
  input  [4:0] AD,
  input  FLUSH,
  input  CLK,
  input  RESET,
  input  ZERO,
  output REG_WRITEo,
  output [1:0] RESULT_SELo,
  output MEM_WRITEo,
  output [2:0] ALU_FUNCo,
  output ALU_SELo,
  output [4:0] AS1o,
  output [4:0] AS2o,
  output [4:0] ADo,
  output PC_SRC
);

  wire and_1_out, or_1_out, register_4_q, register_5_q;

  or or_1 (or_1_out, FLUSH, RESET);
  Register #(.width(1)) register_1 (.D(REG_WRITE), .en(1'b1), .clk(CLK), .Q(REG_WRITEo), .clr(or_1_out));
  Register #(.width(2)) register_2 (.D(RESULT_SEL), .en(1'b1), .clk(CLK), .Q(RESULT_SELo), .clr(or_1_out));
  Register #(.width(1)) register_3 (.D(MEM_WRITE), .en(1'b1), .clk(CLK), .Q(MEM_WRITEo), .clr(or_1_out));
  Register #(.width(1)) register_4 (.D(JUMP), .en(1'b1), .clk(CLK), .Q(register_4_q), .clr(or_1_out));
  Register #(.width(1)) register_5 (.D(BRANCH), .en(1'b1), .clk(CLK), .Q(register_5_q), .clr(or_1_out));
  Register #(.width(3)) register_6 (.D(ALU_FUNC), .en(1'b1), .clk(CLK), .Q(ALU_FUNCo), .clr(or_1_out));
  Register #(.width(1)) register_7 (.D(ALU_SEL), .en(1'b1), .clk(CLK), .Q(ALU_SELo), .clr(or_1_out));
  Register #(.width(5)) register_8 (.D(AS1), .en(1'b1), .clk(CLK), .Q(AS1o), .clr(or_1_out));
  Register #(.width(5)) register_9 (.D(AS2), .en(1'b1), .clk(CLK), .Q(AS2o), .clr(or_1_out));
  Register #(.width(5)) register_10 (.D(AD), .en(1'b1), .clk(CLK), .Q(ADo), .clr(or_1_out));
  and and_1 (and_1_out, register_5_q, ZERO);
  or or_2 (PC_SRC, register_4_q, and_1_out);
endmodule

module execute_data (
  input  [2:0] ALU_FUNC,
  input  ALU_SEL,
  input  [31:0] IMM,
  input  [31:0] S1,
  input  [31:0] S2,
  input  [31:0] PC4,
  input  [31:0] PC,
  input  FLUSH,
  input  CLK,
  input  RESET,
  output ZERO,
  output [31:0] ALU_RESULT,
  output [31:0] WD,
  output [31:0] PC4o,
  output [31:0] TARGET
);

  wire or_1_out;
  wire [31:0] multiplexer_1_out, register_1_q, register_4_q;

  Register #(.width(32)) register_1 (.D(S1), .en(1'b1), .clk(CLK), .Q(register_1_q), .clr(or_1_out));
  Register #(.width(32)) register_2 (.D(S2), .en(1'b1), .clk(CLK), .Q(WD), .clr(or_1_out));
  Register #(.width(32)) register_3 (.D(PC4), .en(1'b1), .clk(CLK), .Q(PC4o), .clr(or_1_out));
  Register #(.width(32)) register_4 (.D(PC), .en(1'b1), .clk(CLK), .Q(register_4_q), .clr(or_1_out));
  or or_1 (or_1_out, FLUSH, RESET);
  Multiplexer #(.width(32)) multiplexer_1 (.in0(IMM), .in1(WD), .out(multiplexer_1_out), .sel(ALU_SEL));
  Adder #(.width(32)) adder_1 (.a(IMM), .b(register_4_q), .out(TARGET), .cin(1'b0));  // open: cout
  execute_alu execute_alu_1 (
    .ALU_CTRL(ALU_FUNC), .S1(register_1_q), .S2(multiplexer_1_out), .ZERO(ZERO), .RESULT(ALU_RESULT));
endmodule

module execute_alu (
  input  [2:0] ALU_CTRL,
  input  [31:0] S1,
  input  [31:0] S2,
  output ZERO,
  output [31:0] RESULT
);

  Comparator #(.width(32)) comparator_1 (.a({32{1'b0}}), .b({32{1'b0}}), .eq(ZERO));  // open: gt, lt

  assign RESULT = {32{1'b0}};
endmodule

module mem_ctrl (
  input  REG_WRITE,
  input  [1:0] RESULT_SEL,
  input  MEM_WRITE,
  input  [4:0] AD,
  input  CLK,
  input  RESET,
  output REG_WRITEo,
  output [1:0] RESULT_SELo,
  output MEM_WRITEo,
  output [4:0] ADo
);

  Register #(.width(1)) register_1 (.D(REG_WRITE), .en(1'b1), .clk(CLK), .Q(REG_WRITEo), .clr(RESET));
  Register #(.width(2)) register_2 (.D(RESULT_SEL), .en(1'b1), .clk(RESET), .Q(RESULT_SELo), .clr(RESET));
  Register #(.width(1)) register_3 (.D(MEM_WRITE), .en(1'b1), .clk(CLK), .Q(MEM_WRITEo), .clr(RESET));
  Register #(.width(5)) register_4 (.D(AD), .en(1'b1), .clk(CLK), .Q(ADo), .clr(RESET));
endmodule

module mem_data (
  input  MEM_WRITE,
  input  [31:0] ALU_RESULT,
  input  [31:0] WD,
  input  [31:0] PC4,
  input  CLK,
  input  RESET,
  output [31:0] ALU_RESULTo,
  output [31:0] RD,
  output [31:0] PC4o
);

  wire [31:0] register_2_q;

  Register #(.width(32)) register_1 (.D(ALU_RESULT), .en(1'b1), .clk(CLK), .Q(ALU_RESULTo), .clr(RESET));
  Register #(.width(32)) register_2 (.D(WD), .en(1'b1), .clk(CLK), .Q(register_2_q), .clr(RESET));
  Register #(.width(32)) register_3 (.D(PC4), .en(1'b1), .clk(CLK), .Q(PC4o), .clr(RESET));
  RAM #(.addrWidth(16), .dataWidth(32), .enables("line")) ram_1 (
    .addr(ALU_RESULTo[15:0]), .we(MEM_WRITE), .clk(CLK), .din(register_2_q), .dout(RD));
endmodule

module wb_ctrl (
  input  REG_WRITE,
  input  [1:0] RESULT_SEL,
  input  [4:0] AD,
  input  CLK,
  input  RESET,
  output REG_WRITEo,
  output [1:0] RESULT_SELo,
  output [4:0] ADo
);

  Register #(.width(1)) register_1 (.D(REG_WRITE), .en(1'b1), .clk(CLK), .Q(REG_WRITEo), .clr(RESET));
  Register #(.width(2)) register_2 (.D(RESULT_SEL), .en(1'b1), .clk(CLK), .Q(RESULT_SELo), .clr(RESET));
  Register #(.width(5)) register_3 (.D(AD), .en(1'b1), .clk(CLK), .Q(ADo), .clr(RESET));
endmodule

module wb_data (
  input  [1:0] RESULT_SEL,
  input  [31:0] ALU_RESULT,
  input  [31:0] RD,
  input  [31:0] PC4,
  input  CLK,
  input  RESET,
  output [31:0] RESULT
);

  wire [31:0] register_1_q, register_2_q;

  Register #(.width(32)) register_1 (.D(RD), .en(1'b1), .clk(CLK), .Q(register_1_q), .clr(RESET));
  Register #(.width(32)) register_2 (.D(PC4), .en(1'b1), .clk(CLK), .Q(register_2_q), .clr(RESET));
  Multiplexer #(.select(2), .width(32)) multiplexer_1 (
    .in0(ALU_RESULT), .in1(register_1_q), .in2(register_2_q), .out(RESULT), .sel(RESULT_SEL));  // open: in3
endmodule
